# Fritzing sketch MAX6675 (saved by Fritzing 0.9.8b)

parts:
  MCU1 = Raspberry Pi Zero
  U4 = POT [package=pot_alpha_rv16af-20]
  U5 = MAX6675 [package=so08]

nets:
  N1: MCU1.pin_1, U5.VDD
  N2: MCU1.pin_6, MCU1.pin_9, U5.VSS
  N3: MCU1.pin_21, U5.MISO
  N4: MCU1.pin_23, U5.SCK
  N5: MCU1.pin_24, U5.CS
  N6: U4.A, U5.T+
  N7: U4.E, U5.T-

notes:
  MAX6675
  K熱
  RaspberryPi ZeroWH
